# Fritzing sketch Connection (saved by Fritzing 0.9.3b)
circuit board: 8.46667cm x 5.64444cm

parts:
  R1 = BBC MicroBit
  IC1 = IC, SIP package, 12 pins [chip_label="BM Lite sensor connector"]

nets:
  N1: R1.GND, IC1.pin7
  N2: R1.3v3, R1.P9_ANALOG_IN, IC1.pin10, IC1.pin11, IC1.pin12
  N3: R1.P15_(MOSI), IC1.pin5
  N4: R1.P14_(MISO), IC1.pin4
  N5: R1.P13_(SCK), IC1.pin6
  N6: R1.P2_-_ANALOG_IN, IC1.pin1
  N7: R1.P1_ANALOG_IN, IC1.pin2
  N8: R1.P0_ANALOG_IN, IC1.pin3

notes:
  Connections from MCU to IC, check documentation for both
  CS PAD2 pin P.01
  Reset PAD1 pin P.02
  IRQ PAD0 pin P.03
  SPI:
  clk 13
  miso 14
  mosi 15

custom parts:
  BBC MicroBit: The BBC MICRO:BIT
